# Fritzing sketch Fritzing Diagram GND-Wires (saved by Fritzing 0.8.7b)
breadboards: 1

parts:
  Pi1 = Adafruit Pi Cobbler
  S1 = Square Green switch [package=ksa_sealed_tac_switch]
  S2 = Square Red switch [package=ksa_sealed_tac_switch]
  S3 = Square Blue switch [package=ksa_sealed_tac_switch]
  S4 = Square Yellow switch [package=ksa_sealed_tac_switch]
  R1 = Resistor [tolerance=±5% resistance=220 package=THT]
  R2 = Resistor [tolerance=±5% resistance=220 package=THT]
  R3 = Resistor [tolerance=±5% resistance=220 package=THT]
  R4 = Resistor [tolerance=±5% resistance=220 package=THT]
  LED1 = LED - 5mm [color="Green (555nm)" package="5 mm [THT]"]
  LED2 = LED - 5mm [color="Red (633nm)" package="5 mm [THT]"]
  LED3 = LED - 5mm [color="Blue (430nm)" package="5 mm [THT]"]
  LED4 = LED - 5mm [color="Yellow (585nm)" package="5 mm [THT]"]

nets:
  N1: Pi1.GND, S1.1, S2.1, S3.1, S4.1, R1.Pin_1, R2.Pin_1, R3.Pin_1, R4.Pin_1
  N2: R1.Pin_0, LED1.cathode
  N3: R2.Pin_0, LED2.cathode
  N4: R3.Pin_0, LED3.cathode
  N5: R4.Pin_0, LED4.cathode

custom parts:
  Adafruit Pi Cobbler: Adafruit Pi Cobbler GPIO Breakout for Raspberry Pi
  Square Green switch: Momentary Switch www.adafruit.com/products/1010
  Square Red switch: Momentary Switch www.adafruit.com/products/1010
  Square Blue switch: Momentary Switch www.adafruit.com/products/1010
  Square Yellow switch: Momentary Switch www.adafruit.com/products/1010
